# Fritzing sketch alarm (saved by Fritzing 0.7.12b)
breadboards: 1
stripboards: 1

parts:
  S1 = Pushbutton [package="[THT]"]
  R1 = Resistor [tolerance=±5% resistance=220 package=THT]
  LED1 = LED - 5mm [color="Red (633nm)" package="5 mm [THT]"]
  J1 = Screw terminal - 2 pins [package=THT]
  Arduino1 = Arduino

nets:
  N1: S1.Pin_1, S1.Pin_2, S1.Pin_3, S1.Pin_4, R1.Pin_1
  N2: R1.Pin_0, LED1.anode
  N3: LED1.cathode, J1.pin1, J1.pin2, Arduino1.A0
