# Fritzing sketch alarm2 (saved by Fritzing 0.7.12b)

parts:
  myScrewShield = Arduino ProtoScrew Shield Kit
  J1 = Infrared Proximity Sensor [part_number=PIR1]

nets:
  5V: myScrewShield.5V, J1.Vcc
  GND: myScrewShield.GND, J1.GND
  N1: myScrewShield.D10, J1.Vout

notes:
  Keypad A0 A7
